// Logisim project ALU.circ as structural Verilog: 1 circuit, main circuit main
module main (
  input  Ainvertt,
  input  Binvert,
  input  CarryIn,
  input  A,
  input  B,
  input  [1:0] Operation,
  output Result,
  output CarryOut
);

  wire adder_1_out, and_1_out, multiplexer_1_out, multiplexer_2_out, not_1_out, not_2_out, or_1_out;

  Multiplexer multiplexer_1 (.in0(A), .in1(not_1_out), .out(multiplexer_1_out), .sel(Ainvertt));  // open: en
  not not_1 (not_1_out, A);
  not not_2 (not_2_out, B);
  Multiplexer multiplexer_2 (.in0(not_2_out), .in1(B), .out(multiplexer_2_out), .sel(Binvert));  // open: en
  or or_1 (or_1_out, multiplexer_1_out, multiplexer_2_out);
  and and_1 (and_1_out, multiplexer_1_out, multiplexer_2_out);
  Adder #(.width(1)) adder_1 (
    .a(multiplexer_1_out), .b(multiplexer_2_out), .out(adder_1_out), .cin(CarryIn), .cout(CarryOut));
  Multiplexer #(.select(2)) multiplexer_3 (
    .in0(or_1_out), .in1(and_1_out), .in2(CarryOut), .in3(adder_1_out), .out(Result), .sel(Operation));  // open: en
  // also tied to VCC on the sheet: CarryOut
endmodule
