// Logisim project DataShift.circ as structural Verilog: 1 circuit, main circuit main
module main (
  input  Shift,
  input  DataShift,
  input  Data,
  output B0,
  output B1,
  output B2,
  output B3
);

  wire and_1_out, and_2_out, and_3_out, clock_1_out, not_1_out, or_1_out;

  Clock clock_1 (.out(clock_1_out));
  not not_1 (not_1_out, DataShift);
  and and_1 (and_1_out, clock_1_out, Shift);
  and and_2 (and_2_out, not_1_out, B3);
  and and_3 (and_3_out, Data, DataShift);
  or or_1 (or_1_out, and_2_out, and_3_out);
  D_Flip_Flop d_ff_1 (.clk(and_1_out), .D(or_1_out), .Q(B0), .en(1'b1));  // open: Qn, preset, reset
  D_Flip_Flop d_ff_2 (.clk(and_1_out), .D(B0), .Q(B1), .en(1'b1));  // open: Qn, preset, reset
  D_Flip_Flop d_ff_3 (.clk(and_1_out), .D(B1), .Q(B2), .en(1'b1));  // open: Qn, preset, reset
  D_Flip_Flop d_ff_4 (.clk(and_1_out), .D(B2), .Q(B3), .en(1'b1));  // open: Qn, preset, reset
endmodule
