// Logisim project carfsm.circ as structural Verilog: 2 circuits, main circuit main
module main (
  input  in_1,
  input  in_2,
  input  in_3,
  input  in_4
);

  wire clock_1_out, d_ff_1_q, not_1_out, or_1_out, or_2_out, state_1_nextstate;

  Clock clock_1 (.out(clock_1_out));
  LED led_1 (.in(d_ff_1_q));
  LED led_2 (.in(d_ff_1_q));
  LED led_3 (.in(not_1_out));
  or or_1 (or_1_out, in_1, in_4);
  LED led_4 (.in(not_1_out));
  or or_2 (or_2_out, in_3, in_2);
  not not_1 (not_1_out, d_ff_1_q);
  state state_1 (.State(d_ff_1_q), .NScar(or_1_out), .EWcar(or_2_out), .NextState(state_1_nextstate));
  D_Flip_Flop d_ff_1 (.clk(clock_1_out), .D(state_1_nextstate), .Q(d_ff_1_q), .en(1'b1));  // open: Qn, preset, reset

  // Notes on the sheet:
  //   NSlite
  //   NScar
  //   EWlite
  //   EWcar
endmodule

module state (
  input  State,
  input  NScar,
  input  EWcar,
  output NextState
);

  wire and_1_out, and_2_out, not_1_out, not_2_out;

  not not_1 (not_1_out, State);
  not not_2 (not_2_out, NScar);
  and and_1 (and_1_out, not_1_out, EWcar);
  and and_2 (and_2_out, State, not_2_out);
  or or_1 (NextState, and_1_out, and_2_out);
endmodule
