// Logisim project holidaylights.circ as structural Verilog: 1 circuit, main circuit main
module main (
  input  Reset
);

  wire clock_1_out, d_ff_1_q, d_ff_2_q, d_ff_3_q, d_ff_4_q, d_ff_5_q, d_ff_6_q, d_ff_7_q, d_ff_8_q;

  Clock clock_1 (.out(clock_1_out));
  D_Flip_Flop d_ff_1 (.clk(clock_1_out), .D(d_ff_8_q), .Q(d_ff_1_q), .preset(Reset), .en(1'b1));  // open: Qn, reset
  LED led_1 (.in(d_ff_1_q));
  LED led_2 (.in(d_ff_2_q));
  D_Flip_Flop d_ff_2 (.clk(clock_1_out), .D(d_ff_1_q), .Q(d_ff_2_q), .en(1'b1), .reset(Reset));  // open: Qn, preset
  LED led_3 (.in(d_ff_3_q));
  D_Flip_Flop d_ff_3 (.clk(clock_1_out), .D(d_ff_2_q), .Q(d_ff_3_q), .en(1'b1), .reset(Reset));  // open: Qn, preset
  LED led_4 (.in(d_ff_4_q));
  D_Flip_Flop d_ff_4 (.clk(clock_1_out), .D(d_ff_3_q), .Q(d_ff_4_q), .en(1'b1), .reset(Reset));  // open: Qn, preset
  LED led_5 (.in(d_ff_5_q));
  D_Flip_Flop d_ff_5 (.clk(clock_1_out), .D(d_ff_4_q), .Q(d_ff_5_q), .en(1'b1), .reset(Reset));  // open: Qn, preset
  LED led_6 (.in(d_ff_6_q));
  D_Flip_Flop d_ff_6 (.clk(clock_1_out), .D(d_ff_5_q), .Q(d_ff_6_q), .en(1'b1), .reset(Reset));  // open: Qn, preset
  LED led_7 (.in(d_ff_7_q));
  D_Flip_Flop d_ff_7 (.clk(clock_1_out), .D(d_ff_6_q), .Q(d_ff_7_q), .en(1'b1), .reset(Reset));  // open: Qn, preset
  LED led_8 (.in(d_ff_8_q));
  D_Flip_Flop d_ff_8 (.clk(clock_1_out), .D(d_ff_7_q), .Q(d_ff_8_q), .en(1'b1), .reset(Reset));  // open: Qn, preset

  // Notes on the sheet:
  //   To use: First, toggle Reset from 0 to 1 to 0
  //   Finally, enable the simulation and enable clock ticks
  //   Next, adjust the clock frequency (e.g., 4 Hz) in the simulation to control the light speed
endmodule
