// Logisim project jrmips-jmm330.circ as structural Verilog: 6 circuits, main circuit 4 Func ALU
module main (
);

  wire ALU_zero, and_1_out, clock_1_out, Control_alusrc, Control_branch, Control_halt, Control_jump,
       Control_memread, Control_memtoreg, Control_memwrite, Control_put, Control_regwrite, Instruction_subop,
       jr_jimmediate, not_1_out;
  wire [2:0] Control_aluop0, Instruction_rs, Instruction_rt;
  wire [3:0] Instruction_opcode, Instruction_shamt, register_1_q, register_1_q_2, register_1_q_3,
       register_1_q_4;
  wire [7:0] adder_1_out, Instruction_immediate, multiplexer_1_out, multiplexer_4_out, multiplexer_5_out,
       PC_q;
  wire [15:0] ALU_result, bit_extender_1_out, bit_extender_2_out, multiplexer_2_out, multiplexer_3_out,
       multiplexer_6_out, ram_1_data, Register_File_read_data_1, Register_File_read_data_2, rom_1_data;

  not not_1 (not_1_out, Control_halt);
  Clock clock_1 (.out(clock_1_out));
  Register PC (.D(multiplexer_5_out), .en(not_1_out), .Q(PC_q), .clk(clock_1_out));  // open: clr
  LED Halt_Check (.in(Control_halt));
  Adder adder_1 (.a(8'h1), .b(PC_q), .out(adder_1_out));  // open: cin, cout
  Hex_Digit_Display hex_digit_display_1 (.value(register_1_q_4));  // open: dp
  Hex_Digit_Display hex_digit_display_2 (.value(register_1_q_3));  // open: dp
  ROM #(.dataWidth(16)) rom_1 (.addr(PC_q), .data(rom_1_data), .sel(1'b1));
  Hex_Digit_Display hex_digit_display_3 (.value(register_1_q_2));  // open: dp
  Hex_Digit_Display hex_digit_display_4 (.value(register_1_q));  // open: dp
  Register #(.width(16)) register_1 (
    .D(Register_File_read_data_1), .en(Control_put),
    .Q({register_1_q_4, register_1_q_3, register_1_q_2, register_1_q}), .clk(clock_1_out));  // open: clr
  Instruction Instruction (
    .Instruction(rom_1_data), .Opcode(Instruction_opcode), .Rs(Instruction_rs), .Rt(Instruction_rt),
    .Shamt(Instruction_shamt), .Immediate(Instruction_immediate), .Subop(Instruction_subop));
  Jump_Control jr (
    .Opcode3(Instruction_opcode[3]), .Opcode2(Instruction_opcode[2]), .Opcode1(Instruction_opcode[1]),
    .Opcode0(Instruction_opcode[0]), .JImmediate(jr_jimmediate));
  Control Control (
    .Opcode3(Instruction_opcode[3]), .Opcode2(Instruction_opcode[2]), .Opcode1(Instruction_opcode[1]),
    .Opcode0(Instruction_opcode[0]), .Subop(Instruction_subop), .Branch(Control_branch),
    .MemRead(Control_memread), .MemToReg(Control_memtoreg), .MemWrite(Control_memwrite),
    .RegWrite(Control_regwrite), .ALUOP2(Control_aluop0[2]), .ALUOP1(Control_aluop0[1]),
    .ALUOP0(Control_aluop0[0]), .ALUSrc(Control_alusrc), .Jump(Control_jump), .Put(Control_put),
    .Halt(Control_halt));
  Register_File Register_File (
    .Read_Register_1(Instruction_rs), .Write_Register(Instruction_rs), .Write_Data(multiplexer_6_out),
    .Read_Register_2(Instruction_rt), .Read_Data_1(Register_File_read_data_1),
    .Read_Data_2(Register_File_read_data_2), .Write_Enable(Control_regwrite), .Clock(clock_1_out));
  Multiplexer #(.width(8), .enable("false")) multiplexer_1 (
    .in0(Register_File_read_data_1[7:0]), .in1(Instruction_immediate), .out(multiplexer_1_out),
    .sel(jr_jimmediate));
  assign bit_extender_1_out = {{8{Instruction_immediate[7]}}, Instruction_immediate};  // Bit_Extender bit_extender_1
  assign bit_extender_2_out = {{8{1'b0}}, Instruction_immediate};  // Bit_Extender bit_extender_2
  Multiplexer #(.width(16), .enable("false")) multiplexer_2 (
    .in0(Register_File_read_data_2), .in1(multiplexer_3_out), .out(multiplexer_2_out), .sel(Control_alusrc));
  Multiplexer #(.width(16), .enable("false")) multiplexer_3 (
    .in0(bit_extender_1_out), .in1(bit_extender_2_out), .out(multiplexer_3_out), .sel(Instruction_subop));
  _4_Func_ALU ALU (
    .A(Register_File_read_data_1), .B(multiplexer_2_out), .Shamt(Instruction_shamt),
    .Operation(Control_aluop0), .Zero(ALU_zero), .Result(ALU_result));
  and and_1 (and_1_out, Control_branch, ALU_zero);
  // Probe on ALU_result
  Multiplexer #(.width(8), .enable("false")) multiplexer_4 (
    .in0(adder_1_out), .in1(Instruction_immediate), .out(multiplexer_4_out), .sel(and_1_out));
  Multiplexer #(.width(8), .enable("false")) multiplexer_5 (
    .in0(multiplexer_4_out), .in1(multiplexer_1_out), .out(multiplexer_5_out), .sel(Control_jump));
  RAM #(.dataWidth(16), .bus("separate")) ram_1 (
    .addr(Register_File_read_data_2[7:0]), .din(Register_File_read_data_1), .data(ram_1_data),
    .str(Control_memwrite), .sel(1'b1), .clk(clock_1_out), .ld(Control_memread));  // open: clr
  Multiplexer #(.width(16), .enable("false")) multiplexer_6 (
    .in0(ALU_result), .in1(ram_1_data), .out(multiplexer_6_out), .sel(Control_memtoreg));

  // Notes on the sheet:
  //   John McQuown
  //   jmm330@pitt.edu
  //   Instruction Memory
  //   contents of rom_1 (hex, n*v repeats v):
  //   2045 2402 4080 7000 6000
  //   rs or imm
  //   addi or addui
  //   rt
  //   rs
  //   PC+1 or Branch
  //   John McQuown
  //   jmm330@pitt.edu
  //   Data Memory
  //   PCorBranch or Jump
endmodule

module _4_Func_ALU (
  input  [15:0] A,
  input  [15:0] B,
  input  [3:0] Shamt,
  input  [2:0] Operation,
  output Zero,
  output [15:0] Result
);

  wire comparator_1_eq, comparator_1_gt, comparator_1_lt, not_1_out;
  wire [15:0] adder_1_out, and_1_out, nor_1_out, shifter_1_out, shifter_2_out, shifter_3_out, shifter_4_out,
       subtractor_1_out;

  assign and_1_out = A & B;  // AND_Gate and_1, 16 bits wide
  assign nor_1_out = ~(A | B);  // NOR_Gate nor_1, 16 bits wide
  Adder #(.width(16)) adder_1 (.a(A), .b(B), .out(adder_1_out));  // open: cin, cout
  Subtractor #(.width(16)) subtractor_1 (.a(A), .b(B), .out(subtractor_1_out));  // open: bin, bout
  Shifter #(.width(16)) shifter_1 (.in(A), .\dist (Shamt), .out(shifter_1_out));
  Shifter #(.width(16), .shift("lr")) shifter_2 (.in(A), .\dist (Shamt), .out(shifter_2_out));
  Shifter #(.width(16)) shifter_3 (.in(A), .\dist (B[3:0]), .out(shifter_3_out));
  Shifter #(.width(16), .shift("lr")) shifter_4 (.in(A), .\dist (B[3:0]), .out(shifter_4_out));
  Multiplexer #(.select(3), .width(16), .enable("false")) multiplexer_1 (
    .in0(and_1_out), .in1(nor_1_out), .in2(adder_1_out), .in3(subtractor_1_out), .in4(shifter_1_out),
    .in5(shifter_2_out), .in6(shifter_3_out), .in7(shifter_4_out), .out(Result), .sel(Operation));
  Comparator #(.width(16)) comparator_1 (
    .a(A), .b({16{1'b0}}), .gt(comparator_1_gt), .eq(comparator_1_eq), .lt(comparator_1_lt));
  not not_1 (not_1_out, comparator_1_eq);
  Multiplexer #(.select(2), .enable("false")) multiplexer_2 (
    .in0(comparator_1_gt), .in1(comparator_1_lt), .in2(not_1_out), .in3(comparator_1_eq), .out(Zero),
    .sel(Operation[1:0]));

  // Notes on the sheet:
  //   sll
  //   srl
  //   sllv
  //   srlv
endmodule

module Register_File (
  input  Write_Enable,
  input  [2:0] Read_Register_1,
  input  [2:0] Write_Register,
  input  [15:0] Write_Data,
  input  [2:0] Read_Register_2,
  input  Clock,
  output [15:0] Read_Data_1,
  output [15:0] Read_Data_2
);

  wire demultiplexer_1_out0, demultiplexer_1_out1, demultiplexer_1_out2, demultiplexer_1_out3,
       demultiplexer_1_out4, demultiplexer_1_out5, demultiplexer_1_out6, demultiplexer_1_out7;
  wire [15:0] register_1_q, register_2_q, register_3_q, register_4_q, register_5_q, register_6_q,
       register_7_q, register_8_q;

  Demultiplexer #(.select(3), .enable("false")) demultiplexer_1 (
    .out0(demultiplexer_1_out0), .out1(demultiplexer_1_out1), .out2(demultiplexer_1_out2),
    .out3(demultiplexer_1_out3), .out4(demultiplexer_1_out4), .out5(demultiplexer_1_out5),
    .out6(demultiplexer_1_out6), .out7(demultiplexer_1_out7), .in(Write_Enable), .sel(Write_Register));
  Register #(.width(16)) register_1 (
    .D(Write_Data), .en(demultiplexer_1_out0), .Q(register_1_q), .clk(Clock));  // open: clr
  Register #(.width(16)) register_2 (
    .D(Write_Data), .en(demultiplexer_1_out1), .Q(register_2_q), .clk(Clock));  // open: clr
  Register #(.width(16)) register_3 (
    .D(Write_Data), .en(demultiplexer_1_out2), .Q(register_3_q), .clk(Clock));  // open: clr
  Register #(.width(16)) register_4 (
    .D(Write_Data), .en(demultiplexer_1_out3), .Q(register_4_q), .clk(Clock));  // open: clr
  Register #(.width(16)) register_5 (
    .D(Write_Data), .en(demultiplexer_1_out4), .Q(register_5_q), .clk(Clock));  // open: clr
  Register #(.width(16)) register_6 (
    .D(Write_Data), .en(demultiplexer_1_out5), .Q(register_6_q), .clk(Clock));  // open: clr
  Register #(.width(16)) register_7 (
    .D(Write_Data), .en(demultiplexer_1_out6), .Q(register_7_q), .clk(Clock));  // open: clr
  Register #(.width(16)) register_8 (
    .D(Write_Data), .en(demultiplexer_1_out7), .Q(register_8_q), .clk(Clock));  // open: clr
  Multiplexer #(.select(3), .width(16), .enable("false")) multiplexer_1 (
    .in0(register_1_q), .in1(register_2_q), .in2(register_3_q), .in3(register_4_q), .in4(register_5_q),
    .in5(register_6_q), .in6(register_7_q), .in7(register_8_q), .out(Read_Data_1), .sel(Read_Register_1));
  Multiplexer #(.select(3), .width(16), .enable("false")) multiplexer_2 (
    .in0(register_1_q), .in1(register_2_q), .in2(register_3_q), .in3(register_4_q), .in4(register_5_q),
    .in5(register_6_q), .in6(register_7_q), .in7(register_8_q), .out(Read_Data_2), .sel(Read_Register_2));
endmodule

module Instruction (
  input  [15:0] Instruction,
  output [3:0] Opcode,
  output [2:0] Rs,
  output [2:0] Rt,
  output [3:0] Shamt,
  output [7:0] Immediate,
  output Subop
);


  assign Immediate = Instruction[8:1];
  assign Opcode = Instruction[15:12];
  assign Rs = Instruction[11:9];
  assign Rt = Instruction[8:6];
  assign Shamt = Instruction[4:1];
  assign Subop = Instruction[0];
endmodule

module Control (
  input  Opcode3,
  input  Opcode2,
  input  Opcode1,
  input  Opcode0,
  input  Subop,
  output Branch,
  output MemRead,
  output MemToReg,
  output MemWrite,
  output RegWrite,
  output ALUOP2,
  output ALUOP1,
  output ALUOP0,
  output ALUSrc,
  output Jump,
  output Put,
  output Halt
);

  wire and_5_out, and_6_out, and_7_out, and_8_out, and_9_out, and_10_out, and_11_out, and_12_out, and_13_out,
       and_14_out, and_15_out, and_16_out, and_17_out, and_18_out, and_19_out, and_20_out, and_21_out,
       not_1_out, not_2_out, not_3_out, not_4_out, not_5_out, not_6_out, not_7_out, not_8_out, not_9_out,
       not_10_out, not_11_out, not_12_out, not_13_out, not_14_out, not_15_out, not_16_out, not_17_out,
       not_18_out, not_19_out, not_20_out, not_21_out, not_22_out, not_23_out, not_24_out, not_25_out,
       not_26_out, not_27_out, not_28_out, not_29_out, not_30_out, not_31_out, not_32_out, not_33_out,
       not_34_out, not_35_out, not_36_out, not_37_out, not_38_out, not_39_out, not_40_out, not_41_out,
       not_42_out, not_43_out, not_44_out, not_45_out;

  not not_1 (not_1_out, Opcode2);
  not not_2 (not_2_out, Opcode3);
  not not_3 (not_3_out, Opcode1);
  not not_4 (not_4_out, Subop);
  not not_5 (not_5_out, Opcode3);
  not not_6 (not_6_out, Opcode1);
  not not_7 (not_7_out, Subop);
  not not_8 (not_8_out, Opcode3);
  not not_9 (not_9_out, Opcode1);
  not not_10 (not_10_out, Opcode3);
  not not_11 (not_11_out, Opcode2);
  not not_12 (not_12_out, Opcode3);
  not not_13 (not_13_out, Opcode1);
  not not_14 (not_14_out, Opcode0);
  not not_15 (not_15_out, Opcode3);
  not not_16 (not_16_out, Opcode1);
  not not_17 (not_17_out, Subop);
  not not_18 (not_18_out, Opcode1);
  not not_19 (not_19_out, Opcode3);
  not not_20 (not_20_out, Opcode2);
  not not_21 (not_21_out, Opcode3);
  not not_22 (not_22_out, Opcode1);
  not not_23 (not_23_out, Opcode0);
  not not_24 (not_24_out, Opcode3);
  not not_25 (not_25_out, Opcode2);
  not not_26 (not_26_out, Opcode1);
  not not_27 (not_27_out, Opcode2);
  not not_28 (not_28_out, Opcode0);
  not not_29 (not_29_out, Opcode3);
  not not_30 (not_30_out, Opcode1);
  not not_31 (not_31_out, Opcode0);
  not not_32 (not_32_out, Opcode2);
  not not_33 (not_33_out, Opcode3);
  not not_34 (not_34_out, Opcode1);
  not not_35 (not_35_out, Opcode0);
  not not_36 (not_36_out, Opcode2);
  not not_37 (not_37_out, Opcode2);
  not not_38 (not_38_out, Opcode2);
  not not_39 (not_39_out, Opcode0);
  not not_40 (not_40_out, Opcode2);
  not not_41 (not_41_out, Opcode1);
  not not_42 (not_42_out, Opcode0);
  not not_43 (not_43_out, Opcode3);
  not not_44 (not_44_out, Opcode3);
  not not_45 (not_45_out, Opcode0);
  and and_1 (Branch, Opcode3, not_1_out);
  and and_2 (MemRead, not_2_out, Opcode2, not_3_out, Opcode0, not_4_out);
  and and_3 (MemToReg, not_5_out, Opcode2, not_6_out, Opcode0, not_7_out);
  and and_4 (MemWrite, not_8_out, Opcode2, not_9_out, Opcode0, Subop);
  and and_5 (and_5_out, not_10_out, not_11_out);
  and and_6 (and_6_out, not_12_out, not_13_out, not_14_out);
  and and_7 (and_7_out, not_15_out, not_16_out, not_17_out);
  and and_8 (and_8_out, Opcode3, Opcode2, not_18_out, Opcode0);
  and and_9 (and_9_out, not_19_out, not_20_out, Opcode1, Opcode0);
  and and_10 (and_10_out, not_21_out, Opcode2, not_22_out, not_23_out);
  and and_11 (and_11_out, not_24_out, not_25_out, not_26_out, Opcode0);
  and and_12 (and_12_out, not_27_out, Opcode1, not_28_out);
  and and_13 (and_13_out, not_29_out, Opcode2, not_30_out, not_31_out);
  and and_14 (and_14_out, Opcode3, not_32_out, Opcode1);
  and and_15 (and_15_out, not_33_out, not_34_out, not_35_out, Subop);
  and and_16 (and_16_out, not_36_out, Opcode0, Subop);
  and and_17 (and_17_out, Opcode3, not_37_out, Opcode0);
  and and_18 (and_18_out, not_38_out, Opcode1, not_39_out);
  and and_19 (and_19_out, Opcode3, not_40_out);
  and and_20 (and_20_out, Opcode3, Opcode2, not_41_out);
  and and_21 (and_21_out, Opcode3, Opcode2, not_42_out);
  and and_22 (Put, not_43_out, Opcode2, Opcode1, Opcode0);
  and and_23 (Halt, not_44_out, Opcode2, Opcode1, not_45_out);
  or or_1 (RegWrite, and_5_out, and_6_out, and_7_out, and_8_out);
  or or_2 (ALUOP2, and_9_out, and_10_out);
  or or_3 (ALUOP1, and_11_out, and_12_out, and_13_out, and_14_out);
  or or_4 (ALUOP0, and_15_out, and_16_out, and_17_out);
  or or_5 (ALUSrc, and_18_out, and_19_out);
  or or_6 (Jump, and_20_out, and_21_out);
endmodule

module Jump_Control (
  input  Opcode3,
  input  Opcode2,
  input  Opcode1,
  input  Opcode0,
  output JImmediate
);

  wire and_1_out, and_2_out, not_1_out, not_2_out;

  not not_1 (not_1_out, Opcode1);
  not not_2 (not_2_out, Opcode0);
  and and_1 (and_1_out, Opcode3, Opcode2, not_1_out, Opcode0);
  and and_2 (and_2_out, Opcode3, Opcode2, Opcode1, not_2_out);
  or or_1 (JImmediate, and_1_out, and_2_out);
endmodule
